// Logisim project inc4_Rip.circ as structural Verilog: 1 circuit, main circuit 4bit_inc_Rip
// 4IncRip
module _4bit_inc_Rip (
  input  Cin,
  input  [3:0] \input ,
  output [3:0] \output ,
  output Cout
);

  wire and_1_out, and_2_out, and_3_out;

  and and_1 (and_1_out, Cin, \input [0]);
  and and_2 (and_2_out, and_1_out, \input [1]);
  and and_3 (and_3_out, and_2_out, \input [2]);
  xor xor_1 (\output [0], Cin, \input [0]);
  xor xor_2 (\output [1], and_1_out, \input [1]);
  xor xor_3 (\output [2], and_2_out, \input [2]);
  xor xor_4 (\output [3], and_3_out, \input [3]);
  and and_4 (Cout, and_3_out, \input [3]);
endmodule
