// Logisim project inc8.circ as structural Verilog: 1 circuit, main circuit main
// inc8
module main (
  input  [7:0] \input ,
  input  [7:0] input_2,
  output [7:0] \output ,
  output [7:0] output_2
);

  wire n4b_inc_la_1_p4, n4bit_inc_rip_1_p4;

  // _4bit_inc_Rip 4bit_inc_rip_1: pin names not known; wires that end beside it: \input [3:0], 1'b1, \output [3:0], n4bit_inc_rip_1_p4
  // _4bit_inc_Rip 4bit_inc_rip_2: pin names not known; wires that end beside it: \input [7:4], n4bit_inc_rip_1_p4, \output [7:4]
  // _4b_inc_LA 4b_inc_la_1: pin names not known; wires that end beside it: input_2[3:0], 1'b1, output_2[3:0], n4b_inc_la_1_p4
  // _4b_inc_LA 4b_inc_la_2: pin names not known; wires that end beside it: input_2[7:4], n4b_inc_la_1_p4, output_2[7:4]

  // Notes on the sheet:
  //   RIPPLE INCREMENTER
  //   LookAhead Incrementer
endmodule
