// Logisim project comparacao_metodos.circ as structural Verilog: 1 circuit, main circuit main
module main (
  input  [15:0] in_1,
  input  [15:0] in_2,
  output [15:0] out_3,
  output [15:0] out_4,
  output [15:0] out_5,
  output [15:0] out_6
);

  wire comparator_1_a_b;

  Conditional_Swapper conditional_swapper_1 (.B(in_1), .A(in_2), .B_2(out_3), .A_2(out_4));  // open: B_A
  comparator comparator_1 (.A_B(comparator_1_a_b), .A(in_2), .B(in_1));
  swap_logic swap_logic_1 (.A(in_2), .B(in_1), .A_B(comparator_1_a_b), .A_2(out_5), .B_2(out_6));
endmodule
