// Logisim project conditional_swapper.circ as structural Verilog: 1 circuit, main circuit Conditional Swapper
// csw
module Conditional_Swapper (
  input  [15:0] B,
  input  [15:0] A,
  output [15:0] B_2,
  output [15:0] A_2
);

  wire comparator_1_p3;

  // comparator comparator_1: pin names not known; wires that end beside it: A, B, comparator_1_p3
  Multiplexer #(.width(16), .enable("false")) multiplexer_1 (.in0(B), .in1(A), .out(B_2), .sel(comparator_1_p3));
  Multiplexer #(.width(16), .enable("false")) multiplexer_2 (.in0(A), .in1(B), .out(A_2), .sel(comparator_1_p3));
endmodule
