// Logisim project michel_comparador.circ as structural Verilog: 1 circuit, main circuit main
module main (
  input  [15:0] B,
  input  [15:0] A,
  output A_B,
  output A_B_2
);

  wire not_1_out, not_2_out, not_3_out, not_4_out, not_5_out, not_6_out, not_7_out, not_8_out, not_9_out,
       not_10_out, not_11_out, not_12_out, not_13_out, not_14_out, not_15_out, not_16_out, or1, or2, or3,
       or4, or5, or6, or7, or8, or9, or10, or11, or12, or13, or14, or15, or16, xnor_1_out, xnor_2_out,
       xnor_3_out, xnor_4_out, xnor_5_out, xnor_6_out, xnor_7_out, xnor_8_out, xnor_9_out, xnor_10_out,
       xnor_11_out, xnor_12_out, xnor_13_out, xnor_14_out, xnor_15_out, xor_1_out, xor_2_out, xor_3_out,
       xor_4_out, xor_5_out, xor_6_out, xor_7_out, xor_8_out, xor_9_out, xor_10_out, xor_11_out, xor_12_out,
       xor_13_out, xor_14_out, xor_15_out, xor_16_out;

  nor nor_1 (A_B_2, xor_1_out, xor_2_out, xor_3_out, xor_4_out, xor_5_out, xor_6_out, xor_7_out, xor_8_out, xor_9_out, xor_10_out, xor_11_out, xor_12_out, xor_13_out, xor_14_out, xor_15_out, xor_16_out);
  xor xor_1 (xor_1_out, B[15], A[15]);
  xor xor_2 (xor_2_out, B[14], A[14]);
  xor xor_3 (xor_3_out, B[13], A[13]);
  xor xor_4 (xor_4_out, B[12], A[12]);
  xor xor_5 (xor_5_out, B[11], A[11]);
  xor xor_6 (xor_6_out, B[10], A[10]);
  xor xor_7 (xor_7_out, B[9], A[9]);
  xor xor_8 (xor_8_out, B[8], A[8]);
  xor xor_9 (xor_9_out, B[7], A[7]);
  xor xor_10 (xor_10_out, B[6], A[6]);
  xor xor_11 (xor_11_out, B[5], A[5]);
  xor xor_12 (xor_12_out, B[4], A[4]);
  xor xor_13 (xor_13_out, B[3], A[3]);
  xor xor_14 (xor_14_out, B[2], A[2]);
  xor xor_15 (xor_15_out, B[1], A[1]);
  xor xor_16 (xor_16_out, B[0], A[0]);
  not not_1 (not_1_out, A[15]);
  not not_2 (not_2_out, A[14]);
  not not_3 (not_3_out, A[11]);
  not not_4 (not_4_out, A[7]);
  not not_5 (not_5_out, A[6]);
  not not_6 (not_6_out, A[10]);
  not not_7 (not_7_out, A[12]);
  not not_8 (not_8_out, A[8]);
  not not_9 (not_9_out, A[13]);
  not not_10 (not_10_out, A[9]);
  not not_11 (not_11_out, A[2]);
  not not_12 (not_12_out, A[0]);
  not not_13 (not_13_out, A[5]);
  not not_14 (not_14_out, A[1]);
  not not_15 (not_15_out, A[3]);
  not not_16 (not_16_out, A[4]);
  and and_1 (or1, not_1_out, B[15]);
  xnor xnor_1 (xnor_1_out, B[15], A[15]);
  or or_1 (A_B, or1, or2, or3, or4, or5, or6, or7, or8, or9, or10, or11, or12, or13, or14, or15, or16);
  and and_2 (or2, B[14], xnor_1_out, not_2_out);
  xnor xnor_2 (xnor_2_out, B[14], A[14]);
  and and_3 (or3, xnor_1_out, B[13], xnor_2_out, not_9_out);
  xnor xnor_3 (xnor_3_out, B[13], A[13]);
  and and_4 (or4, xnor_1_out, xnor_2_out, B[12], xnor_3_out, not_7_out);
  xnor xnor_4 (xnor_4_out, B[12], A[12]);
  xnor xnor_5 (xnor_5_out, B[11], A[11]);
  and and_5 (or5, xnor_1_out, xnor_2_out, xnor_3_out, B[11], xnor_4_out, not_3_out);
  and and_6 (or6, xnor_1_out, xnor_2_out, xnor_3_out, xnor_4_out, B[10], xnor_5_out, not_6_out);
  xnor xnor_6 (xnor_6_out, B[10], A[10]);
  xnor xnor_7 (xnor_7_out, B[9], A[9]);
  and and_7 (or7, xnor_1_out, xnor_2_out, xnor_3_out, xnor_4_out, xnor_5_out, B[9], xnor_6_out, not_10_out);
  xnor xnor_8 (xnor_8_out, B[8], A[8]);
  and and_8 (or8, xnor_1_out, xnor_2_out, xnor_3_out, xnor_4_out, xnor_5_out, xnor_6_out, B[8], xnor_7_out, not_8_out);
  xnor xnor_9 (xnor_9_out, B[7], A[7]);
  and and_9 (or9, xnor_1_out, xnor_2_out, xnor_3_out, xnor_4_out, xnor_5_out, xnor_6_out, xnor_7_out, B[7], xnor_8_out, not_4_out);
  xnor xnor_10 (xnor_10_out, B[6], A[6]);
  xnor xnor_11 (xnor_11_out, B[5], A[5]);
  and and_10 (or10, xnor_1_out, xnor_2_out, xnor_3_out, xnor_4_out, xnor_5_out, xnor_6_out, xnor_7_out, xnor_8_out, B[6], xnor_9_out, not_5_out);
  xnor xnor_12 (xnor_12_out, B[4], A[4]);
  xnor xnor_13 (xnor_13_out, B[3], A[3]);
  and and_11 (or11, xnor_1_out, xnor_2_out, xnor_3_out, xnor_4_out, xnor_5_out, xnor_6_out, xnor_7_out, xnor_8_out, xnor_9_out, B[5], xnor_10_out, not_13_out);
  xnor xnor_14 (xnor_14_out, B[2], A[2]);
  xnor xnor_15 (xnor_15_out, B[1], A[1]);
  and and_12 (or12, xnor_1_out, xnor_2_out, xnor_3_out, xnor_4_out, xnor_5_out, xnor_6_out, xnor_7_out, xnor_8_out, xnor_9_out, xnor_10_out, B[4], xnor_11_out, not_16_out);
  and and_13 (or13, xnor_1_out, xnor_2_out, xnor_3_out, xnor_4_out, xnor_5_out, xnor_6_out, xnor_7_out, xnor_8_out, xnor_9_out, xnor_10_out, xnor_11_out, B[3], xnor_12_out, not_15_out);
  and and_14 (or14, xnor_1_out, xnor_2_out, xnor_3_out, xnor_4_out, xnor_5_out, xnor_6_out, xnor_7_out, xnor_8_out, xnor_9_out, xnor_10_out, xnor_11_out, xnor_12_out, B[2], xnor_13_out, not_11_out);
  and and_15 (or15, xnor_1_out, xnor_2_out, xnor_3_out, xnor_4_out, xnor_5_out, xnor_6_out, xnor_7_out, xnor_8_out, xnor_9_out, xnor_10_out, xnor_11_out, xnor_12_out, xnor_13_out, B[1], xnor_14_out, not_14_out);
  and and_16 (or16, xnor_1_out, xnor_2_out, xnor_3_out, xnor_4_out, xnor_5_out, xnor_6_out, xnor_7_out, xnor_8_out, xnor_9_out, xnor_10_out, xnor_11_out, xnor_12_out, xnor_13_out, xnor_14_out, B[0], xnor_15_out, not_12_out);

  // Other names for the same wires on the sheet: _0 = B[0]; _1 = B[1]; _2 = B[2]; _3 = B[3]; _4 = B[4]; _5 = B[5];
  //   _6 = B[6]; _7 = B[7]; _8 = B[8]; _9 = B[9]; _10 = B[10]; _11 = B[11]; _12 = B[12]; _13 = B[13]; _14 = B[14];
  //   _15 = B[15]
endmodule
