// Logisim project old_sorter.circ as structural Verilog: 4 circuits, main circuit Main
module Ctrl (
  input  all_ok,
  input  reset,
  input  clk,
  output [1:0] sel,
  output done
);

  wire and_2_out, and_3_out, and_4_out, and_5_out, and_6_out, and_7_out, and_8_out, and_9_out, and_10_out,
       not_1_out, not_2_out, not_3_out, not_4_out, not_5_out, not_6_out, not_7_out, not_8_out, not_9_out,
       not_10_out;
  wire [1:0] or_3_out;
  wire [1:1] state_reg_q;

  not not_1 (not_1_out, state_reg_q[1]);
  not not_2 (not_2_out, sel[0]);
  not not_3 (not_3_out, state_reg_q[1]);
  not not_4 (not_4_out, reset);
  not not_5 (not_5_out, sel[0]);
  not not_6 (not_6_out, sel[0]);
  not not_7 (not_7_out, reset);
  not not_8 (not_8_out, state_reg_q[1]);
  not not_9 (not_9_out, sel[0]);
  not not_10 (not_10_out, reset);
  and and_1 (done, state_reg_q[1], sel[0]);
  and and_2 (and_2_out, not_1_out, not_2_out);
  and and_3 (and_3_out, state_reg_q[1], sel[0]);
  and and_4 (and_4_out, not_3_out, sel[0]);
  and and_5 (and_5_out, sel[0], not_4_out);
  and and_6 (and_6_out, state_reg_q[1], not_5_out, all_ok);
  and and_7 (and_7_out, not_6_out, not_7_out);
  and and_8 (and_8_out, not_8_out, sel[0], all_ok);
  and and_9 (and_9_out, state_reg_q[1], not_9_out);
  and and_10 (and_10_out, state_reg_q[1], not_10_out);
  or or_1 (sel[1], and_2_out, and_3_out);
  or or_2 (or_3_out[1], and_4_out, and_5_out, and_6_out);
  or or_3 (or_3_out[0], and_7_out, and_8_out, and_9_out, and_10_out);
  Register #(.width(2)) state_reg (.D(or_3_out), .Q({state_reg_q[1], sel[0]}), .clk(clk));  // open: en, clr
endmodule

module Data (
  input  [15:0] input0,
  input  [15:0] input1,
  input  [15:0] input2,
  input  [15:0] input3,
  input  [15:0] input4,
  input  [15:0] input5,
  input  [15:0] input6,
  input  [15:0] input7,
  input  [15:0] input8,
  input  [15:0] input9,
  input  [1:0] select,
  input  clk,
  output [15:0] B0,
  output all_ok,
  output [15:0] B1,
  output [15:0] B2,
  output [15:0] B3,
  output [15:0] B4,
  output [15:0] B5,
  output [15:0] B6,
  output [15:0] B7,
  output [15:0] B8,
  output [15:0] B9
);

  wire d_ff_1_q, main_1_p3, main_1_p5, main_1_p6, main_3_p3, main_4_p3, main_5_p3, nor_1_out;
  wire [15:0] multiplexer_1_out, multiplexer_2_out, multiplexer_3_out, multiplexer_4_out, multiplexer_5_out,
       multiplexer_6_out, multiplexer_7_out, multiplexer_8_out, multiplexer_9_out, multiplexer_10_out,
       multiplexer_11_out, multiplexer_12_out, multiplexer_13_out, multiplexer_14_out, multiplexer_15_out,
       multiplexer_16_out, multiplexer_17_out, multiplexer_18_out, multiplexer_19_out, swap_logic_1_a_2,
       swap_logic_1_b_2, swap_logic_2_a_2, swap_logic_2_b_2, swap_logic_3_a_2, swap_logic_3_b_2,
       swap_logic_4_a_2, swap_logic_4_b_2, swap_logic_5_a_2, swap_logic_5_b_2;

  Multiplexer #(.select(2), .width(16), .disabled(0), .enable("false")) multiplexer_1 (
    .in0(swap_logic_2_b_2), .in1(swap_logic_2_a_2), .in2(input2), .out(multiplexer_1_out), .sel(select));  // open: in3
  Multiplexer #(.select(2), .width(16), .disabled(0), .enable("false")) multiplexer_2 (
    .in0(swap_logic_3_b_2), .in1(swap_logic_3_a_2), .in2(input4), .out(multiplexer_2_out), .sel(select));  // open: in3
  Multiplexer #(.select(2), .width(16), .disabled(0), .enable("false")) multiplexer_3 (
    .in0(swap_logic_4_b_2), .in1(swap_logic_4_a_2), .in2(input6), .out(multiplexer_3_out), .sel(select));  // open: in3
  Multiplexer #(.select(2), .width(16), .disabled(0), .enable("false")) multiplexer_4 (
    .in0(swap_logic_5_b_2), .in1(swap_logic_5_a_2), .in2(input8), .out(multiplexer_4_out), .sel(select));  // open: in3
  Multiplexer #(.width(16), .enable("false")) multiplexer_5 (
    .in0(swap_logic_1_b_2), .in1(input0), .out(multiplexer_5_out), .sel(select[1]));
  Multiplexer #(.select(2), .width(16), .disabled(0), .enable("false")) multiplexer_6 (
    .in0(swap_logic_1_a_2), .in1(swap_logic_2_b_2), .in2(input1), .out(multiplexer_6_out), .sel(select));  // open: in3
  Multiplexer #(.select(2), .width(16), .disabled(0), .enable("false")) multiplexer_7 (
    .in0(swap_logic_2_a_2), .in1(swap_logic_3_b_2), .in2(input3), .out(multiplexer_7_out), .sel(select));  // open: in3
  Multiplexer #(.select(2), .width(16), .disabled(0), .enable("false")) multiplexer_8 (
    .in0(swap_logic_3_a_2), .in1(swap_logic_4_b_2), .in2(input5), .out(multiplexer_8_out), .sel(select));  // open: in3
  Multiplexer #(.select(2), .width(16), .disabled(0), .enable("false")) multiplexer_9 (
    .in0(swap_logic_4_a_2), .in1(swap_logic_5_b_2), .in2(input7), .out(multiplexer_9_out), .sel(select));  // open: in3
  Multiplexer #(.select(2), .width(16), .disabled(0), .enable("false")) multiplexer_10 (
    .in0(swap_logic_5_a_2), .in1(swap_logic_1_a_2), .in2(input9), .out(multiplexer_10_out), .sel(select));  // open: in3
  Register #(.width(16)) A0 (.D(multiplexer_5_out), .Q(B0), .clk(clk));  // open: en, clr
  Register #(.width(16)) A1 (.D(multiplexer_6_out), .Q(B1), .clk(clk));  // open: en, clr
  Register #(.width(16)) A2 (.D(multiplexer_1_out), .Q(B2), .clk(clk));  // open: en, clr
  Register #(.width(16)) A3 (.D(multiplexer_7_out), .Q(B3), .clk(clk));  // open: en, clr
  Register #(.width(16)) A4 (.D(multiplexer_2_out), .Q(B4), .clk(clk));  // open: en, clr
  Register #(.width(16)) A5 (.D(multiplexer_8_out), .Q(B5), .clk(clk));  // open: en, clr
  Register #(.width(16)) A6 (.D(multiplexer_3_out), .Q(B6), .clk(clk));  // open: en, clr
  Register #(.width(16)) A7 (.D(multiplexer_9_out), .Q(B7), .clk(clk));  // open: en, clr
  Register #(.width(16)) A8 (.D(multiplexer_4_out), .Q(B8), .clk(clk));  // open: en, clr
  Register #(.width(16)) A9 (.D(multiplexer_10_out), .Q(B9), .clk(clk));  // open: en, clr
  Multiplexer #(.width(16), .enable("false")) multiplexer_11 (
    .in0(B1), .in1(B9), .out(multiplexer_11_out), .sel(select[0]));
  Multiplexer #(.width(16), .enable("false")) multiplexer_12 (
    .in0(B2), .in1(B1), .out(multiplexer_12_out), .sel(select[0]));
  Multiplexer #(.width(16), .enable("false")) multiplexer_13 (
    .in0(B3), .in1(B2), .out(multiplexer_13_out), .sel(select[0]));
  Multiplexer #(.width(16), .enable("false")) multiplexer_14 (
    .in0(B4), .in1(B3), .out(multiplexer_14_out), .sel(select[0]));
  Multiplexer #(.width(16), .enable("false")) multiplexer_15 (
    .in0(B5), .in1(B4), .out(multiplexer_15_out), .sel(select[0]));
  Multiplexer #(.width(16), .enable("false")) multiplexer_16 (
    .in0(B6), .in1(B5), .out(multiplexer_16_out), .sel(select[0]));
  Multiplexer #(.width(16), .enable("false")) multiplexer_17 (
    .in0(B7), .in1(B6), .out(multiplexer_17_out), .sel(select[0]));
  Multiplexer #(.width(16), .enable("false")) multiplexer_18 (
    .in0(B8), .in1(B7), .out(multiplexer_18_out), .sel(select[0]));
  Multiplexer #(.width(16), .enable("false")) multiplexer_19 (
    .in0(B9), .in1(B8), .out(multiplexer_19_out), .sel(select[0]));
  // comparador_main main_1: pin names not known; wires that end beside it: multiplexer_11_out, B0, main_1_p3, multiplexer_13_out, main_1_p5, main_1_p6
  // comparador_main main_2: pin names not known; wires that end beside it: multiplexer_11_out, B0, main_1_p3, multiplexer_13_out, multiplexer_12_out, main_1_p5, main_1_p6
  // comparador_main main_3: pin names not known; wires that end beside it: multiplexer_15_out, multiplexer_14_out, main_3_p3
  // comparador_main main_4: pin names not known; wires that end beside it: multiplexer_17_out, multiplexer_16_out, main_4_p3
  // comparador_main main_5: pin names not known; wires that end beside it: multiplexer_19_out, multiplexer_18_out, main_5_p3
  swap_logic swap_logic_1 (
    .A(multiplexer_11_out), .B(B0), .A_B(main_1_p5), .A_2(swap_logic_1_a_2), .B_2(swap_logic_1_b_2));
  nor nor_1 (nor_1_out, main_1_p5, main_1_p6, main_3_p3, main_4_p3, main_5_p3);
  D_Flip_Flop d_ff_1 (.clk(clk), .D(nor_1_out), .Q(d_ff_1_q));  // open: Qn, preset, en, reset
  swap_logic swap_logic_2 (
    .A(multiplexer_13_out), .B(multiplexer_12_out), .A_B(main_1_p6), .A_2(swap_logic_2_a_2),
    .B_2(swap_logic_2_b_2));
  swap_logic swap_logic_3 (
    .A(multiplexer_15_out), .B(multiplexer_14_out), .A_B(main_3_p3), .A_2(swap_logic_3_a_2),
    .B_2(swap_logic_3_b_2));
  and and_1 (all_ok, d_ff_1_q, nor_1_out);
  swap_logic swap_logic_4 (
    .A(multiplexer_17_out), .B(multiplexer_16_out), .A_B(main_4_p3), .A_2(swap_logic_4_a_2),
    .B_2(swap_logic_4_b_2));
  swap_logic swap_logic_5 (
    .A(multiplexer_19_out), .B(multiplexer_18_out), .A_B(main_5_p3), .A_2(swap_logic_5_a_2),
    .B_2(swap_logic_5_b_2));

  // Other names for the same wires on the sheet: clock = clk; odd_even = select[0]; sel[1:0] = select;
  //   A0_sel = select[1]
endmodule

// swp
module swap_logic (
  input  [15:0] A,
  input  A_B,
  input  [15:0] B,
  output [15:0] A_2,
  output [15:0] B_2
);

  Multiplexer #(.width(16), .enable("false")) multiplexer_1 (.in0(A), .in1(B), .out(A_2), .sel(A_B));
  Multiplexer #(.width(16), .enable("false")) multiplexer_2 (.in0(B), .in1(A), .out(B_2), .sel(A_B));
endmodule

module Main (
  input  [15:0] in_1,
  input  [15:0] in_2,
  input  [15:0] in_3,
  input  [15:0] in_4,
  input  [15:0] in_5,
  input  rst,
  input  [15:0] in_7,
  input  [15:0] in_8,
  input  [15:0] in_9,
  input  [15:0] in_10,
  input  [15:0] in_11,
  output [15:0] out_12,
  output [15:0] out_13,
  output [15:0] out_14,
  output done,
  output [15:0] out_16,
  output [15:0] out_17,
  output [15:0] out_18,
  output [15:0] out_19,
  output [15:0] out_20,
  output [15:0] out_21,
  output [15:0] out_22
);

  wire clock_1_out, data_1_all_ok;
  wire [1:0] ctrl_1_sel;

  Data data_1 (
    .input0(in_1), .input1(in_2), .input2(in_3), .input3(in_4), .input4(in_5), .input5(in_7), .input6(in_8),
    .input7(in_9), .input8(in_10), .input9(in_11), .select(ctrl_1_sel), .clk(clock_1_out), .B0(out_12),
    .all_ok(data_1_all_ok), .B1(out_13), .B2(out_14), .B3(out_16), .B4(out_17), .B5(out_18), .B6(out_19),
    .B7(out_20), .B8(out_21), .B9(out_22));
  Clock clock_1 (.out(clock_1_out));
  Ctrl ctrl_1 (.all_ok(data_1_all_ok), .reset(rst), .sel(ctrl_1_sel), .done(done), .clk(clock_1_out));
endmodule
