// Logisim project test_csw.circ as structural Verilog: 2 circuits, main circuit main
module main (
  input  [15:0] A,
  input  [15:0] B,
  output [15:0] A_2,
  output [15:0] B_2,
  output out_5
);

  comparator comparator_1 (.A_B(out_5), .A(B), .B(A));
  swap_logic swap_logic_1 (.A(B), .B(A), .A_B(out_5), .A_2(A_2), .B_2(B_2));
endmodule

// swp
module swap_logic (
  input  [15:0] A,
  input  A_B,
  input  [15:0] B,
  output [15:0] A_2,
  output [15:0] B_2
);

  Multiplexer #(.width(16), .enable("false")) multiplexer_1 (.in0(A), .in1(B), .out(A_2), .sel(A_B));
  Multiplexer #(.width(16), .enable("false")) multiplexer_2 (.in0(B), .in1(A), .out(B_2), .sel(A_B));
endmodule
