// Logisim project sorter.circ as structural Verilog: 1 circuit, main circuit Data
module Data (
  input  rst,
  input  [15:0] input0,
  input  [15:0] input1,
  input  [15:0] input2,
  input  [15:0] input3,
  input  [15:0] input4,
  input  [15:0] input5,
  input  [15:0] input6,
  input  [15:0] input7,
  input  [15:0] input8,
  input  [15:0] input9,
  output rdy,
  output [15:0] output0,
  output [15:0] output1,
  output [15:0] output2,
  output [15:0] output3,
  output [15:0] output4,
  output [15:0] output5,
  output [15:0] output6,
  output [15:0] output7,
  output [15:0] output8,
  output [15:0] output9
);

  wire C0, C0_e_o, C0_ne_o, C1, C1_ne_o, C2, C2_ne_o, C3, C3_ne_o, C4, C4_ne_o, clk, d_ff_2_q, d_ff_3_q,
       d_ff_4_qn, E0, E1, E2, E3, E4, e_o, nC1_e_o_nE1, nC2_e_o_nE2, nC3_e_o_nE3, nC4_e_o_nE4, ne_o,
       nor_1_out, not_1_out, not_2_out, not_4_out, reset;
  wire [15:0] adder_1_out, cycle_count, multiplexer_1_out, multiplexer_2_out, multiplexer_3_out,
       multiplexer_4_out, multiplexer_5_out, multiplexer_6_out, multiplexer_7_out, multiplexer_8_out,
       multiplexer_9_out, multiplexer_10_out, multiplexer_17_out, multiplexer_18_out, multiplexer_19_out,
       multiplexer_20_out, multiplexer_21_out, multiplexer_22_out, multiplexer_23_out, multiplexer_24_out,
       multiplexer_25_out, R0, R1, R2, R3, R4, R5, R6, R7, R8, R9, R13, R35, R57, R79, R91;

  D_Flip_Flop #(.enable("true")) d_ff_1 (.clk(clk), .D(rst), .Q(reset));  // open: Qn, preset, en, reset
  not not_1 (not_1_out, rdy);
  Register #(.width(16)) register_1 (.D(adder_1_out), .en(not_1_out), .Q(cycle_count), .clk(clk), .clr(reset));
  Adder #(.width(16)) adder_1 (.a(16'h1), .b(cycle_count), .out(adder_1_out));  // open: cin, cout
  // Probe on cycle_count
  Multiplexer #(.width(16), .disabled(0), .enable("false")) multiplexer_1 (
    .in0(output0), .in1(input0), .out(multiplexer_1_out), .sel(reset));
  Multiplexer #(.width(16), .disabled(0), .enable("false")) multiplexer_2 (
    .in0(output1), .in1(input1), .out(multiplexer_2_out), .sel(reset));
  Multiplexer #(.width(16), .disabled(0), .enable("false")) multiplexer_3 (
    .in0(output2), .in1(input2), .out(multiplexer_3_out), .sel(reset));
  Multiplexer #(.width(16), .disabled(0), .enable("false")) multiplexer_4 (
    .in0(output3), .in1(input3), .out(multiplexer_4_out), .sel(reset));
  Multiplexer #(.width(16), .disabled(0), .enable("false")) multiplexer_5 (
    .in0(output4), .in1(input4), .out(multiplexer_5_out), .sel(reset));
  Multiplexer #(.width(16), .disabled(0), .enable("false")) multiplexer_6 (
    .in0(output5), .in1(input5), .out(multiplexer_6_out), .sel(reset));
  Multiplexer #(.width(16), .disabled(0), .enable("false")) multiplexer_7 (
    .in0(output6), .in1(input6), .out(multiplexer_7_out), .sel(reset));
  Multiplexer #(.width(16), .disabled(0), .enable("false")) multiplexer_8 (
    .in0(output7), .in1(input7), .out(multiplexer_8_out), .sel(reset));
  Multiplexer #(.width(16), .disabled(0), .enable("false")) multiplexer_9 (
    .in0(output8), .in1(input8), .out(multiplexer_9_out), .sel(reset));
  Multiplexer #(.width(16), .disabled(0), .enable("false")) multiplexer_10 (
    .in0(output9), .in1(input9), .out(multiplexer_10_out), .sel(reset));
  Register #(.width(16)) u_R0 (.D(multiplexer_1_out), .Q(R0), .clk(clk));  // open: en, clr
  Register #(.width(16)) A1 (.D(multiplexer_2_out), .Q(R1), .clk(clk));  // open: en, clr
  Register #(.width(16)) A2 (.D(multiplexer_3_out), .Q(R2), .clk(clk));  // open: en, clr
  Register #(.width(16)) A3 (.D(multiplexer_4_out), .Q(R3), .clk(clk));  // open: en, clr
  Register #(.width(16)) A4 (.D(multiplexer_5_out), .Q(R4), .clk(clk));  // open: en, clr
  Register #(.width(16)) A5 (.D(multiplexer_6_out), .Q(R5), .clk(clk));  // open: en, clr
  Register #(.width(16)) A6 (.D(multiplexer_7_out), .Q(R6), .clk(clk));  // open: en, clr
  Register #(.width(16)) A7 (.D(multiplexer_8_out), .Q(R7), .clk(clk));  // open: en, clr
  Register #(.width(16)) A8 (.D(multiplexer_9_out), .Q(R8), .clk(clk));  // open: en, clr
  Register #(.width(16)) A9 (.D(multiplexer_10_out), .Q(R9), .clk(clk));  // open: en, clr
  Multiplexer #(.width(16), .enable("false")) multiplexer_11 (.in0(R9), .in1(R1), .out(R91), .sel(e_o));
  Multiplexer #(.width(16), .enable("false")) multiplexer_12 (.in0(R1), .in1(R3), .out(R13), .sel(e_o));
  Multiplexer #(.width(16), .enable("false")) multiplexer_13 (.in0(R3), .in1(R5), .out(R35), .sel(e_o));
  Multiplexer #(.width(16), .enable("false")) multiplexer_14 (.in0(R5), .in1(R7), .out(R57), .sel(e_o));
  Multiplexer #(.width(16), .enable("false")) multiplexer_15 (.in0(R7), .in1(R9), .out(R79), .sel(e_o));
  comparador_main main_1 (.A_B(C0), .A(R91), .B(R0), .A_B_2(E0));
  comparador_main main_2 (.A_B(C1), .A(R2), .B(R13), .A_B_2(E1));
  comparador_main main_3 (.A_B(C2), .A(R4), .B(R35), .A_B_2(E2));
  comparador_main main_4 (.A_B(C3), .A(R6), .B(R57), .A_B_2(E3));
  comparador_main main_5 (.A_B(C4), .A(R8), .B(R79), .A_B_2(E4));
  Multiplexer #(.width(16), .enable("false")) multiplexer_16 (.in0(R0), .in1(R91), .out(output0), .sel(C0));
  Multiplexer #(.width(16), .enable("false")) multiplexer_17 (
    .in0(R1), .in1(R2), .out(multiplexer_17_out), .sel(C1_ne_o));
  Multiplexer #(.width(16), .enable("false")) multiplexer_18 (
    .in0(R2), .in1(R1), .out(multiplexer_18_out), .sel(C1_ne_o));
  Multiplexer #(.width(16), .enable("false")) multiplexer_19 (
    .in0(R3), .in1(R4), .out(multiplexer_19_out), .sel(C2_ne_o));
  Multiplexer #(.width(16), .enable("false")) multiplexer_20 (
    .in0(R4), .in1(R3), .out(multiplexer_20_out), .sel(C2_ne_o));
  Multiplexer #(.width(16), .enable("false")) multiplexer_21 (
    .in0(R5), .in1(R6), .out(multiplexer_21_out), .sel(C3_ne_o));
  Multiplexer #(.width(16), .enable("false")) multiplexer_22 (
    .in0(R6), .in1(R5), .out(multiplexer_22_out), .sel(C3_ne_o));
  Multiplexer #(.width(16), .enable("false")) multiplexer_23 (
    .in0(R7), .in1(R8), .out(multiplexer_23_out), .sel(C4_ne_o));
  Multiplexer #(.width(16), .enable("false")) multiplexer_24 (
    .in0(R8), .in1(R7), .out(multiplexer_24_out), .sel(C4_ne_o));
  Multiplexer #(.width(16), .enable("false")) multiplexer_25 (
    .in0(R9), .in1(R0), .out(multiplexer_25_out), .sel(C0_ne_o));
  Multiplexer #(.width(16), .enable("false")) multiplexer_26 (
    .in0(multiplexer_17_out), .in1(R0), .out(output1), .sel(C0_e_o));
  Multiplexer #(.width(16), .enable("false")) multiplexer_27 (
    .in0(multiplexer_18_out), .in1(R3), .out(output2), .sel(nC1_e_o_nE1));
  Multiplexer #(.width(16), .enable("false")) multiplexer_28 (
    .in0(multiplexer_19_out), .in1(R2), .out(output3), .sel(nC1_e_o_nE1));
  Multiplexer #(.width(16), .enable("false")) multiplexer_29 (
    .in0(multiplexer_20_out), .in1(R5), .out(output4), .sel(nC2_e_o_nE2));
  Multiplexer #(.width(16), .enable("false")) multiplexer_30 (
    .in0(multiplexer_21_out), .in1(R4), .out(output5), .sel(nC2_e_o_nE2));
  Multiplexer #(.width(16), .enable("false")) multiplexer_31 (
    .in0(multiplexer_22_out), .in1(R7), .out(output6), .sel(nC3_e_o_nE3));
  Multiplexer #(.width(16), .enable("false")) multiplexer_32 (
    .in0(multiplexer_23_out), .in1(R6), .out(output7), .sel(nC3_e_o_nE3));
  Multiplexer #(.width(16), .enable("false")) multiplexer_33 (
    .in0(multiplexer_24_out), .in1(R9), .out(output8), .sel(nC4_e_o_nE4));
  Multiplexer #(.width(16), .enable("false")) multiplexer_34 (
    .in0(multiplexer_25_out), .in1(R8), .out(output9), .sel(nC4_e_o_nE4));
  nor nor_1 (nor_1_out, C0, C1_ne_o, C2_ne_o, C3_ne_o, C4_ne_o, nC1_e_o_nE1, nC2_e_o_nE2, nC3_e_o_nE3, nC4_e_o_nE4);
  not not_2 (not_2_out, rdy);
  D_Flip_Flop #(.enable("true")) d_ff_2 (
    .clk(clk), .D(1'b1), .Q(d_ff_2_q), .en(not_2_out), .reset(rst));  // open: Qn, preset
  and and_1 (C0_ne_o, C0, ~e_o);  // AND_Gate
  and and_2 (C1_ne_o, C1, ~e_o);  // AND_Gate
  and and_3 (C2_ne_o, C2, ~e_o);  // AND_Gate
  and and_4 (C3_ne_o, C3, ~e_o);  // AND_Gate
  and and_5 (C4_ne_o, C4, ~e_o);  // AND_Gate
  D_Flip_Flop d_ff_3 (.clk(clk), .D(nor_1_out), .Q(d_ff_3_q), .reset(rst));  // open: Qn, preset
  and and_6 (rdy, d_ff_3_q, d_ff_2_q);
  and and_7 (C0_e_o, C0, e_o);
  and and_8 (nC1_e_o_nE1, ~C1, e_o, ~E1);  // AND_Gate
  and and_9 (nC2_e_o_nE2, ~C2, e_o, ~E2);  // AND_Gate
  and and_10 (nC3_e_o_nE3, ~C3, e_o, ~E3);  // AND_Gate
  and and_11 (nC4_e_o_nE4, ~C4, e_o, ~E4);  // AND_Gate
  Clock clock_1 (.out(clk));
  not not_3 (ne_o, e_o);
  not not_4 (not_4_out, rdy);
  D_Flip_Flop #(.enable("true")) d_ff_4 (
    .clk(clk), .D(d_ff_4_qn), .Q(e_o), .Qn(d_ff_4_qn), .en(not_4_out), .reset(reset));  // open: preset

  // Other names for the same wires on the sheet: R22[15:0] = R2; R44[15:0] = R4; R66[15:0] = R6; R88[15:0] = R8;
  //   ready = rdy; swap0[15:0] = output0; swap1[15:0] = output1; swap2[15:0] = output2; swap3[15:0] = output3;
  //   swap4[15:0] = output4; swap5[15:0] = output5; swap6[15:0] = output6; swap7[15:0] = output7;
  //   swap8[15:0] = output8; swap9[15:0] = output9
endmodule
