// Logisim project inc4_LA.circ as structural Verilog: 1 circuit, main circuit 4b_inc_LA
// 4IncLA
module _4b_inc_LA (
  input  Cin,
  input  [3:0] \input ,
  output [3:0] \output ,
  output Cout
);

  wire and_1_out, and_2_out, and_3_out;

  and and_1 (and_1_out, Cin, \input [0]);
  and and_2 (and_2_out, Cin, \input [0], \input [1]);
  and and_3 (and_3_out, Cin, \input [0], \input [1], \input [2]);
  and and_4 (Cout, Cin, \input [0], \input [1], \input [2], \input [3]);
  xor xor_1 (\output [0], Cin, \input [0]);
  xor xor_2 (\output [1], and_1_out, \input [1]);
  xor xor_3 (\output [2], and_2_out, \input [2]);
  xor xor_4 (\output [3], and_3_out, \input [3]);
endmodule
